# Fritzing sketch sensor_controller_battery (saved by Fritzing 0.8.5b)
breadboards: 1

parts:
  VCC1 = Battery
  U6 = Mystery Part - 8 pins [chip_label=ESP8266 package=THT]
  U7 = attiny85 [package=dip]
  DS5 = DS18B20 1-Wire Temperature Sensor [part_number=DS18B20]
  R27 = Resistor [tolerance=±5% resistance=4.7k package=THT]
  Q8 = Basic FET N-Channel [package="TO220 [THT]"]
  D14 = Rectifier Diode [part_number=1N4001 package="Melf DO-213 AB [SMD]"]  # not connected
  C4 = Ceramic Capacitor [capacitance=1µF package="100 mil [THT, multilayer]"]
  R28 = Resistor [tolerance=±5% resistance=10k package=THT]
  R29 = Resistor [tolerance=±5% resistance=10k package=THT]
  C6 = Ceramic Capacitor [capacitance=1µF package="100 mil [THT, multilayer]"]
  U8 = mystery part, 3 pins [chip_label=MCP170]
  R31 = Resistor [tolerance=±5% resistance=10k package=THT]

nets:
  N1: VCC1.-, U7.Pin_4, Q8.source, C4.0, C6.0, U8.pin1, R31.Pin_1
  N2: VCC1.+, C6.1, U8.pin2
  3.3V: U6.CHPD/Enable, U6.3.3V, U7.Pin_8, DS5.VDD, R27.Pin_0, C4.1, R28.Pin_1, R29.Pin_1, U8.pin3
  N3: U6.RST, U7.Pin_2, R28.Pin_0
  N4: U6.GPIO0, DS5.DQ, R27.Pin_1
  N5: U6.GPIO2, U7.Pin_7
  GND: U6.GND, DS5.GND, Q8.drain
  N6: U7.Pin_1, R29.Pin_0
  N7: U7.Pin_6, Q8.gate, R31.Pin_0

notes:
  Only needed for (1,7)

custom parts:
  Mystery Part - 8 pins: A dummy, proxy, ersatz, stand-in part for whatever you want. With 8 pins on a 300mil inline pin header footprint.
